// Digital circuit 8bitcpu.dig as structural Verilog
module _8bitcpu (
  input  CLK_MAIN,
  input  CLK_DISPLAY
);

  wire button_2_out, CLK, decoder_1_out_0, decoder_1_out_1, decoder_1_out_2, decoder_1_out_3, DISPFLE,
       DISPLE, OLE, RST, TMLE;
  wire [3:0] OADDR;
  wire [7:0] LUTDISP_d, register_with_clear_2_q, register_with_clear_3_q, register_with_clear_4_q,
       register_with_clear_5_q, undriven;
  wire [10:0] register_with_clear_1_q;

  Button button_1 (.out(RST));
  Button button_2 (.out(button_2_out));
  Demultiplexer #(.Selector_Bits(4)) demultiplexer_1 (
    .sel(OADDR), .in(OLE), .out_0(DISPLE), .out_1(DISPFLE), .out_2(TMLE));  // open: out_3, out_4, out_5, out_6, out_7, out_8, out_9, out_10, out_11, out_12, out_13, out_14, out_15
  // SwitchDT switchdt_1: pin names not known; wires that end beside it: CLK_MAIN, button_2_out, CLK
  core core_1 (.CLK(CLK), .RST(RST), .BUS(undriven), .OUTLE(OLE), .EADDR(OADDR));
  register_with_clear register_with_clear_1 (
    .D(undriven), .CLK(CLK), .CLR(RST), .LE(DISPLE), .Q(register_with_clear_1_q[7:0]));
  Register register_1 (.D(undriven[0]), .C(CLK), .en(DISPFLE), .Q(register_with_clear_1_q[10]));
  Terminal terminal_1 (.D(undriven), .C(CLK), .en(TMLE));
  Counter #(.Bits(2)) CNTSEVENSEG (
    .en(1'b1), .C(CLK_DISPLAY), .clr(decoder_1_out_3), .out(register_with_clear_1_q[9:8]));  // open: ovf
  EEPROM #(.AddrBits(13), .isProgramMemory("true"), .Bits(8)) LUTDISP (
    .A({2'b00, register_with_clear_1_q}), .CS(~1'b0), .WE(~1'b1), .OE(~1'b0), .D(LUTDISP_d));
  Decoder #(.Selector_Bits(2)) decoder_1 (
    .sel(register_with_clear_1_q[9:8]), .out_0(decoder_1_out_0), .out_1(decoder_1_out_1),
    .out_2(decoder_1_out_2), .out_3(decoder_1_out_3));
  Seven_Seg #(.ledPersistence("true"), .commonConnectionType("anode")) seven_seg_1 (
    .a(register_with_clear_2_q[0]), .b(register_with_clear_2_q[1]), .c(register_with_clear_2_q[2]),
    .d(register_with_clear_2_q[3]), .e(register_with_clear_2_q[4]), .f(register_with_clear_2_q[5]),
    .g(register_with_clear_2_q[6]), .dp(register_with_clear_2_q[7]));
  register_with_clear register_with_clear_2 (
    .D(LUTDISP_d), .CLK(CLK_DISPLAY), .CLR(RST), .LE(decoder_1_out_3), .Q(register_with_clear_2_q));
  Seven_Seg #(.ledPersistence("true"), .commonConnectionType("anode")) seven_seg_2 (
    .a(register_with_clear_3_q[0]), .b(register_with_clear_3_q[1]), .c(register_with_clear_3_q[2]),
    .d(register_with_clear_3_q[3]), .e(register_with_clear_3_q[4]), .f(register_with_clear_3_q[5]),
    .g(register_with_clear_3_q[6]), .dp(register_with_clear_3_q[7]));
  register_with_clear register_with_clear_3 (
    .D(LUTDISP_d), .CLK(CLK_DISPLAY), .CLR(RST), .LE(decoder_1_out_2), .Q(register_with_clear_3_q));
  Seven_Seg #(.ledPersistence("true"), .commonConnectionType("anode")) seven_seg_3 (
    .a(register_with_clear_4_q[0]), .b(register_with_clear_4_q[1]), .c(register_with_clear_4_q[2]),
    .d(register_with_clear_4_q[3]), .e(register_with_clear_4_q[4]), .f(register_with_clear_4_q[5]),
    .g(register_with_clear_4_q[6]), .dp(register_with_clear_4_q[7]));
  register_with_clear register_with_clear_4 (
    .D(LUTDISP_d), .CLK(CLK_DISPLAY), .CLR(RST), .LE(decoder_1_out_1), .Q(register_with_clear_4_q));
  Seven_Seg #(.ledPersistence("true"), .commonConnectionType("anode")) seven_seg_4 (
    .a(register_with_clear_5_q[0]), .b(register_with_clear_5_q[1]), .c(register_with_clear_5_q[2]),
    .d(register_with_clear_5_q[3]), .e(register_with_clear_5_q[4]), .f(register_with_clear_5_q[5]),
    .g(register_with_clear_5_q[6]), .dp(register_with_clear_5_q[7]));
  register_with_clear register_with_clear_5 (
    .D(LUTDISP_d), .CLK(CLK_DISPLAY), .CLR(RST), .LE(decoder_1_out_0), .Q(register_with_clear_5_q));

  // Other names for the same wires on the sheet: CLK_DISP = CLK_DISPLAY

  // Notes on the sheet:
  //   CLK_MAIN: Hz: 1000
  //   CLK_DISPLAY: Hz: 240
  //   contents of LUTDISP (hex, n*v repeats v):
  //   3f,6,5b,4f,66,6d,7d,7,7f,6f,3f,6,5b,4f,66,6d,7d,7,7f,6f,3f,6,5b,4f,66,6d,7d,7,7f,
  //   6f,3f,6,5b,4f,66,6d,7d,7,7f,6f,3f,6,5b,4f,66,6d,7d,7,7f,6f,3f,6,5b,4f,66,6d,7d,7,
  //   7f,6f,3f,6,5b,4f,66,6d,7d,7,7f,6f,3f,6,5b,4f,66,6d,7d,7,7f,6f,3f,6,5b,4f,66,6d,7d,
  //   7,7f,6f,3f,6,5b,4f,66,6d,7d,7,7f,6f,3f,6,5b,4f,66,6d,7d,7,7f,6f,3f,6,5b,4f,66,6d,
  //   7d,7,7f,6f,3f,6,5b,4f,66,6d,7d,7,7f,6f,3f,6,5b,4f,66,6d,7d,7,7f,6f,3f,6,5b,4f,66,
  //   6d,7d,7,7f,6f,3f,6,5b,4f,66,6d,7d,7,7f,6f,3f,6,5b,4f,66,6d,7d,7,7f,6f,3f,6,5b,4f,
  //   66,6d,7d,7,7f,6f,3f,6,5b,4f,66,6d,7d,7,7f,6f,3f,6,5b,4f,66,6d,7d,7,7f,6f,3f,6,5b,
  //   4f,66,6d,7d,7,7f,6f,3f,6,5b,4f,66,6d,7d,7,7f,6f,3f,6,5b,4f,66,6d,7d,7,7f,6f,3f,6,
  //   5b,4f,66,6d,7d,7,7f,6f,3f,6,5b,4f,66,6d,7d,7,7f,6f,3f,6,5b,4f,66,6d,3f,3f,3f,3f,3f,
  //   3f,3f,3f,3f,3f,6,6,6,6,6,6,6,6,6,6,5b,5b,5b,5b,5b,5b,5b,5b,5b,5b,4f,4f,4f,4f,4f,4f,
  //   4f,4f,4f,4f,66,66,66,66,66,66,66,66,66,66,6d,6d,6d,6d,6d,6d,6d,6d,6d,6d,7d,7d,7d,
  //   7d,7d,7d,7d,7d,7d,7d,7,7,7,7,7,7,7,7,7,7,7f,7f,7f,7f,7f,7f,7f,7f,7f,7f,6f,6f,6f,6f,
  //   6f,6f,6f,6f,6f,6f,3f,3f,3f,3f,3f,3f,3f,3f,3f,3f,6,6,6,6,6,6,6,6,6,6,5b,5b,5b,5b,5b,
  //   5b,5b,5b,5b,5b,4f,4f,4f,4f,4f,4f,4f,4f,4f,4f,66,66,66,66,66,66,66,66,66,66,6d,6d,
  //   6d,6d,6d,6d,6d,6d,6d,6d,7d,7d,7d,7d,7d,7d,7d,7d,7d,7d,7,7,7,7,7,7,7,7,7,7,7f,7f,7f,
  //   7f,7f,7f,7f,7f,7f,7f,6f,6f,6f,6f,6f,6f,6f,6f,6f,6f,3f,3f,3f,3f,3f,3f,3f,3f,3f,3f,
  //   6,6,6,6,6,6,6,6,6,6,5b,5b,5b,5b,5b,5b,5b,5b,5b,5b,4f,4f,4f,4f,4f,4f,4f,4f,4f,4f,66,
  //   66,66,66,66,66,66,66,66,66,6d,6d,6d,6d,6d,6d,3f,3f,3f,3f,3f,3f,3f,3f,3f,3f,3f,3f,
  //   3f,3f,3f,3f,3f,3f,3f,3f,3f,3f,3f,3f,3f,3f,3f,3f,3f,3f,3f,3f,3f,3f,3f,3f,3f,3f,3f,
  //   3f,3f,3f,3f,3f,3f,3f,3f,3f,3f,3f,3f,3f,3f,3f,3f,3f,3f,3f,3f,3f,3f,3f,3f,3f,3f,3f,
  //   3f,3f,3f,3f,3f,3f,3f,3f,3f,3f,3f,3f,3f,3f,3f,3f,3f,3f,3f,3f,3f,3f,3f,3f,3f,3f,3f,
  //   3f,3f,3f,3f,3f,3f,3f,6,6,6,6,6,6,6,6,6,6,6,6,6,6,6,6,6,6,6,6,6,6,6,6,6,6,6,6,6,6,
  //   6,6,6,6,6,6,6,6,6,6,6,6,6,6,6,6,6,6,6,6,6,6,6,6,6,6,6,6,6,6,6,6,6,6,6,6,6,6,6,6,6,
  //   6,6,6,6,6,6,6,6,6,6,6,6,6,6,6,6,6,6,6,6,6,6,6,6,6,6,6,6,6,5b,5b,5b,5b,5b,5b,5b,5b,
  //   5b,5b,5b,5b,5b,5b,5b,5b,5b,5b,5b,5b,5b,5b,5b,5b,5b,5b,5b,5b,5b,5b,5b,5b,5b,5b,5b,
  //   5b,5b,5b,5b,5b,5b,5b,5b,5b,5b,5b,5b,5b,5b,5b,5b,5b,5b,5b,5b,5b,0,0,0,0,0,0,0,0,0,
  //   0,0,0,0,0,0,0,0,0,0,0,0,0,0,0,0,0,0,0,0,0,0,0,0,0,0,0,0,0,0,0,0,0,0,0,0,0,0,0,0,0,
  //   0,0,0,0,0,0,0,0,0,0,0,0,0,0,0,0,0,0,0,0,0,0,0,0,0,0,0,0,0,0,0,0,0,0,0,0,0,0,0,0,0,
  //   0,0,0,0,0,0,0,0,0,0,0,0,0,0,0,0,0,0,0,0,0,0,0,0,0,0,0,0,0,0,0,0,0,0,0,0,0,0,0,0,0,
  //   0,0,0,0,0,0,0,0,0,0,0,0,0,0,0,0,0,0,0,0,0,0,0,0,0,0,0,0,0,0,0,0,0,0,0,0,0,0,0,0,0,
  //   0,0,0,0,0,0,0,0,0,0,0,0,0,0,0,0,0,0,0,0,0,0,0,0,0,0,0,0,0,0,0,0,0,0,0,0,0,0,0,0,0,
  //   0,0,0,0,0,0,0,0,0,0,0,0,0,0,0,0,0,0,0,0,0,0,0,0,0,0,0,0,0,0,0,0,0,0,0,0,0,0,0,0,0,
  //   0,3f,6,5b,4f,66,6d,7d,7,7f,6f,3f,6,5b,4f,66,6d,7d,7,7f,6f,3f,6,5b,4f,66,6d,7d,7,7f,
  //   6f,3f,6,5b,4f,66,6d,7d,7,7f,6f,3f,6,5b,4f,66,6d,7d,7,7f,6f,3f,6,5b,4f,66,6d,7d,7,
  //   7f,6f,3f,6,5b,4f,66,6d,7d,7,7f,6f,3f,6,5b,4f,66,6d,7d,7,7f,6f,3f,6,5b,4f,66,6d,7d,
  //   7,7f,6f,3f,6,5b,4f,66,6d,7d,7,7f,6f,3f,6,5b,4f,66,6d,7d,7,7f,6f,3f,6,5b,4f,66,6d,
  //   7d,7,7f,6f,3f,6,5b,4f,66,6d,7d,7,7f,7,7d,6d,66,4f,5b,6,3f,6f,7f,7,7d,6d,66,4f,5b,
  //   6,3f,6f,7f,7,7d,6d,66,4f,5b,6,3f,6f,7f,7,7d,6d,66,4f,5b,6,3f,6f,7f,7,7d,6d,66,4f,
  //   5b,6,3f,6f,7f,7,7d,6d,66,4f,5b,6,3f,6f,7f,7,7d,6d,66,4f,5b,6,3f,6f,7f,7,7d,6d,66,
  //   4f,5b,6,3f,6f,7f,7,7d,6d,66,4f,5b,6,3f,6f,7f,7,7d,6d,66,4f,5b,6,3f,6f,7f,7,7d,6d,
  //   66,4f,5b,6,3f,6f,7f,7,7d,6d,66,4f,5b,6,3f,6f,7f,7,7d,6d,66,4f,5b,6,3f,3f,3f,3f,3f,
  //   3f,3f,3f,3f,3f,6,6,6,6,6,6,6,6,6,6,5b,5b,5b,5b,5b,5b,5b,5b,5b,5b,4f,4f,4f,4f,4f,4f,
  //   4f,4f,4f,4f,66,66,66,66,66,66,66,66,66,66,6d,6d,6d,6d,6d,6d,6d,6d,6d,6d,7d,7d,7d,
  //   7d,7d,7d,7d,7d,7d,7d,7,7,7,7,7,7,7,7,7,7,7f,7f,7f,7f,7f,7f,7f,7f,7f,7f,6f,6f,6f,6f,
  //   6f,6f,6f,6f,6f,6f,3f,3f,3f,3f,3f,3f,3f,3f,3f,3f,6,6,6,6,6,6,6,6,6,6,5b,5b,5b,5b,5b,
  //   5b,5b,5b,5b,5b,5b,5b,5b,5b,5b,5b,5b,6,6,6,6,6,6,6,6,6,6,3f,3f,3f,3f,3f,3f,3f,3f,3f,
  //   3f,6f,6f,6f,6f,6f,6f,6f,6f,6f,6f,7f,7f,7f,7f,7f,7f,7f,7f,7f,7f,7,7,7,7,7,7,7,7,7,
  //   7,7d,7d,7d,7d,7d,7d,7d,7d,7d,7d,6d,6d,6d,6d,6d,6d,6d,6d,6d,6d,66,66,66,66,66,66,66,
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endmodule
